// Logisim project VHDL_2_homework.circ as structural Verilog
module main (
  input  in_1,
  input  in_2,
  input  in_3,
  input  in_4,
  input  [7:0] in_5,
  input  [2:0] in_6,
  input  [2:0] in_7,
  input  in_8,
  input  in_9,
  input  in_10,
  input  in_11,
  input  in_12,
  input  in_13,
  input  in_14,
  input  in_15,
  input  in_16,
  input  in_17,
  input  in_18,
  input  in_19,
  input  in_20,
  input  in_21,
  input  in_22,
  input  in_23,
  input  in_24,
  input  in_25,
  input  in_26,
  input  in_27,
  input  in_28,
  input  in_29,
  input  in_30,
  input  in_31,
  input  in_32,
  input  in_33,
  input  in_34,
  input  in_35,
  input  in_36,
  input  in_37,
  input  in_38,
  input  in_39,
  input  in_40,
  input  in_41,
  input  in_42,
  input  in_43,
  input  in_44,
  input  in_45,
  input  in_46,
  output out_47,
  output out_48,
  output out_49,
  output out_50
);

  wire [6:0] ones_counter_seg_1_seg, seg_letters_1_seg;

  problem1 problem1_1 (.a(in_1), .b(in_2), .c(in_3), .d(in_4), .out1(out_47), .out2(out_48));
  mux8to1 mux8to1_1 (.d(in_5), .sel(in_6), .y(out_49));
  voting25 voting25_1 (
    .votes({in_8, in_9, in_10, in_11, in_12, in_13, in_14, in_15, in_16, in_17, in_18, in_19, in_20, in_21, in_22, in_23, in_24, in_25, in_26, in_27, in_28, in_29, in_30, in_31, in_32}),
    .pass(out_50));
  seg_letters seg_letters_1 (.sel(in_7), .seg(seg_letters_1_seg));
  _7_Segment_Display u_7_segment_display_1 (
    .g(seg_letters_1_seg[6]), .f(seg_letters_1_seg[5]), .a(seg_letters_1_seg[0]), .b(seg_letters_1_seg[1]),
    .e(seg_letters_1_seg[4]), .d(seg_letters_1_seg[3]), .c(seg_letters_1_seg[2]));  // open: dp
  ones_counter_seg ones_counter_seg_1 (
    .vt({in_33, in_34, in_35, in_36, in_37, in_38, in_39, in_40, in_41, in_42, in_43, in_44, in_45}),
    .en(in_46), .seg(ones_counter_seg_1_seg));
  _7_Segment_Display u_7_segment_display_2 (
    .g(ones_counter_seg_1_seg[6]), .f(ones_counter_seg_1_seg[5]), .a(ones_counter_seg_1_seg[0]),
    .b(ones_counter_seg_1_seg[1]), .e(ones_counter_seg_1_seg[4]), .d(ones_counter_seg_1_seg[3]),
    .c(ones_counter_seg_1_seg[2]));  // open: dp
endmodule

// VHDL entity problem1, as the project stores it:
library ieee;
use ieee.std_logic_1164.all;

entity problem1 is
    port (
        a    : in  std_logic;
        b    : in  std_logic;
        c    : in  std_logic;
        d    : in  std_logic;
        out1 : out std_logic;
        out2 : out std_logic
    );
end problem1;

architecture behavioral of problem1 is
begin
    out1 <= a and b and c and d;
    out2 <= a or b or c or d;
end behavioral;

// VHDL entity mux8to1, as the project stores it:
library ieee;
use ieee.std_logic_1164.all;

entity mux8to1 is
    port (
        d   : in  std_logic_vector(7 downto 0);
        sel : in  std_logic_vector(2 downto 0);
        y   : out std_logic
    );
end mux8to1;

architecture behavioral of mux8to1 is
begin
    with sel select
        y <= d(0) when "000",
             d(1) when "001",
             d(2) when "010",
             d(3) when "011",
             d(4) when "100",
             d(5) when "101",
             d(6) when "110",
             d(7) when "111",
             '0'  when others;
end behavioral;

// VHDL entity seg_letters, as the project stores it:
library ieee;
use ieee.std_logic_1164.all;

entity seg_letters is
    port (
        sel : in  std_logic_vector(2 downto 0);
        seg : out std_logic_vector(6 downto 0) -- gfedcba
    );
end seg_letters;

architecture behavioral of seg_letters is
begin
    process(sel)
    begin
        -- 비트 순서: "gfedcba" (1: 켜짐, 0: 꺼짐)
        case sel is
            when "000" => seg <= "1110111"; -- A
            when "001" => seg <= "1111100"; -- b
            when "010" => seg <= "0111001"; -- C
            when "011" => seg <= "1011110"; -- d
            when "100" => seg <= "1110001"; -- F
            when "101" => seg <= "0111101"; -- G
            when others => seg <= "0000000"; -- OFF
        end case;
    end process;
end behavioral;

// VHDL entity voting25, as the project stores it:
library ieee;
use ieee.std_logic_1164.all;
use ieee.numeric_std.all;

entity voting25 is
    port (
        votes : in  std_logic_vector(24 downto 0);
        pass  : out std_logic
    );
end voting25;

architecture behavioral of voting25 is
begin
    process(votes)
        variable cnt : integer range 0 to 25;
    begin
        cnt := 0;
        for i in 0 to 24 loop
            if votes(i) = '1' then
                cnt := cnt + 1;
            end if;
        end loop;

        if cnt >= 13 then
            pass <= '1';
        else
            pass <= '0';
        end if;
    end process;
end behavioral;

// VHDL entity ones_counter_seg, as the project stores it:
library ieee;
use ieee.std_logic_1164.all;
use ieee.numeric_std.all;

entity ones_counter_seg is
    port (
        vt  : in  std_logic_vector(12 downto 0);
        en  : in  std_logic;
        seg : out std_logic_vector(6 downto 0)
    );
end ones_counter_seg;

architecture behavioral of ones_counter_seg is
begin
    process(vt, en)
        variable cnt : integer range 0 to 15;
    begin
        cnt := 0;
        for i in 0 to 12 loop
            if vt(i) = '1' then
                cnt := cnt + 1;
            end if;
        end loop;

        if en = '0' then
            seg <= "0000000"; -- en='0'이면 화면 끔
        else
            case cnt is
                when 0  => seg <= "0111111"; -- 0
                when 1  => seg <= "0000110"; -- 1
                when 2  => seg <= "1011011"; -- 2
                when 3  => seg <= "1001111"; -- 3
                when 4  => seg <= "1100110"; -- 4
                when 5  => seg <= "1101101"; -- 5
                when 6  => seg <= "1111101"; -- 6
                when 7  => seg <= "0000111"; -- 7
                when 8  => seg <= "1111111"; -- 8
                when 9  => seg <= "1101111"; -- 9
                when 10 => seg <= "1110111"; -- A
                when 11 => seg <= "1111100"; -- b
                when 12 => seg <= "0111001"; -- C
                when 13 => seg <= "1011110"; -- d
                when 14 => seg <= "1111001"; -- E
                when 15 => seg <= "1110001"; -- F
                when others => seg <= "0000000";
            end case;
        end if;
    end process;
end behavioral;
