// Logisim project d_ff_async_complete.circ as structural Verilog
module main (
  input  v_clk,
  input  v_d,
  input  v_clr,
  input  v_set,
  input  D_3,
  input  clk_2,
  input  clr,
  input  set,
  output v_q,
  output q_4,
  output n_complete_q
);

  wire nand_1_out, nand_2_out, nand_3_out, nand_4_out, nand_5_out, nand_6_out, nand_7_out, not_1_out,
       not_2_out, not_3_out;

  not not_1 (not_1_out, D_3);
  not not_2 (not_2_out, clk_2);
  not not_3 (not_3_out, clr);
  nand nand_1 (nand_1_out, D_3, not_2_out);
  nand nand_2 (nand_2_out, not_2_out, not_1_out);
  nand nand_3 (nand_3_out, not_3_out, set);
  d_ff_async d_ff (.clk(v_clk), .d(v_d), .clr(v_clr), .set(v_set), .q(v_q));
  nand nand_4 (nand_4_out, nand_3_out, nand_1_out, nand_5_out);
  nand nand_5 (nand_5_out, nand_4_out, nand_2_out, not_3_out);
  nand nand_6 (nand_6_out, nand_4_out, clk_2);
  nand nand_7 (nand_7_out, clk_2, nand_5_out);
  nand nand_8 (q_4, nand_3_out, nand_6_out, n_complete_q);
  nand nand_9 (n_complete_q, q_4, nand_7_out, not_3_out);
endmodule

// VHDL entity d_ff_async, as the project stores it:
LIBRARY ieee;
USE ieee.std_logic_1164.ALL;

ENTITY d_ff_async IS
    PORT (
        clk : IN  std_logic;
        d   : IN  std_logic;
        clr : IN  std_logic;
        set : IN  std_logic;
        q   : OUT std_logic
    );
END d_ff_async;

ARCHITECTURE bhv OF d_ff_async IS
    SIGNAL q_int : std_logic := '0';
BEGIN
    q <= q_int;

    PROCESS (clk, clr, set)
    BEGIN
        -- 1순위: 비동기 Clear (클럭 무관 즉시 0)
        IF (clr = '1') THEN
            q_int <= '0';
        -- 2순위: 비동기 Set (클럭 무관 즉시 1)
        ELSIF (set = '1') THEN
            q_int <= '1';
        -- 3순위: 동기 D Flip-Flop 동작 (클럭 상승 에지)
        ELSIF rising_edge(clk) THEN
            q_int <= d;
        END IF;
    END PROCESS;
END bhv;
