// Logisim project not_gate.circ as structural Verilog
module main (
  input  in_1,
  output out_2
);

  not_gate not_gate_1 (.a(in_1), .y(out_2));
endmodule

// VHDL entity not_gate, as the project stores it:
--------------------------------------------------------------------------------
-- Project :
-- File    :
-- Autor   :
-- Date    :
--
--------------------------------------------------------------------------------
-- Description :
--
--------------------------------------------------------------------------------

LIBRARY ieee;
USE ieee.std_logic_1164.all;

ENTITY not_gate IS
  PORT(
  	a : in std_logic;
  	y : out std_logic
  );
END not_gate;

--------------------------------------------------------------------------------
--Complete your VHDL description below
--------------------------------------------------------------------------------

ARCHITECTURE TypeArchitecture OF not_gate IS

BEGIN
	y <= not a;
END TypeArchitecture;
