// Logisim project work_1234.circ as structural Verilog
module main (
  input  in_1,
  input  in_2,
  input  s,
  input  r,
  input  in_5,
  input  in_6,
  input  D,
  input  en,
  input  in_9,
  input  in_10,
  input  d_1,
  input  clk,
  input  in_13,
  input  in_14,
  input  in_15,
  input  J,
  input  CLK_1,
  input  in_18,
  input  K,
  output out_20,
  output out_21,
  output nq,
  output q,
  output out_24,
  output q_1,
  output out_26,
  output out_27,
  output out_28,
  output out_29,
  output out_30,
  output out_31,
  output q_3,
  output complete_q_3
);

  wire nand_1_out, nand_2_out, nand_5_out, nand_6_out, nand_7_out, nand_8_out, nand_9_out, nand_13_out,
       nand_14_out, not_1_out, not_2_out, not_3_out, not_4_out, not_5_out;

  not not_1 (not_1_out, D);
  nand nand_1 (nand_1_out, D, en);
  nand nand_2 (nand_2_out, en, not_1_out);
  rs_latch rs_latch_1 (.s(in_1), .r(in_2), .q(out_20), .nq(out_21));
  nor nor_1 (nq, s, q);
  nor nor_2 (q, nq, r);
  not not_2 (not_2_out, d_1);
  not not_3 (not_3_out, clk);
  d_latch d_latch_1 (.en(in_5), .d(in_6), .q(out_24));
  nand nand_3 (q_1, nand_1_out, out_26);
  nand nand_4 (out_26, q_1, nand_2_out);
  nand nand_5 (nand_5_out, d_1, clk);
  nand nand_6 (nand_6_out, clk, not_2_out);
  nand nand_7 (nand_7_out, complete_q_3, J, CLK_1);
  nand nand_8 (nand_8_out, CLK_1, K, q_3);
  nand nand_9 (nand_9_out, nand_5_out, out_29);
  nand nand_10 (out_29, nand_9_out, nand_6_out);
  not not_4 (not_4_out, not_3_out);
  not not_5 (not_5_out, nand_9_out);
  nand nand_11 (q_3, nand_7_out, complete_q_3);
  nand nand_12 (complete_q_3, q_3, in_18, nand_8_out);
  d_ff d_ff_1 (.clk(in_9), .d(in_10), .q(out_27));
  nand nand_13 (nand_13_out, nand_9_out, not_4_out);
  nand nand_14 (nand_14_out, not_4_out, not_5_out);
  jk_ff jk_ff_1 (.clk(in_13), .j(in_14), .k(in_15), .q(out_31));
  nand nand_15 (out_28, nand_13_out, out_30);
  nand nand_16 (out_30, out_28, nand_14_out);
endmodule

// VHDL entity rs_latch, as the project stores it:
LIBRARY ieee;
USE ieee.std_logic_1164.ALL;

ENTITY rs_latch IS
    PORT (
        s  : IN  std_logic;
        r  : IN  std_logic;
        q  : OUT std_logic;
        nq : OUT std_logic
    );
END rs_latch;

ARCHITECTURE bhv OF rs_latch IS
    SIGNAL q_int, nq_int : std_logic;
BEGIN
    q_int  <= r NOR nq_int;
    nq_int <= s NOR q_int;
    q      <= q_int;
    nq     <= nq_int;
END bhv;

// VHDL entity d_latch, as the project stores it:
LIBRARY ieee;
USE ieee.std_logic_1164.ALL;

ENTITY d_latch IS
    PORT (
        en : IN  std_logic;
        d  : IN  std_logic;
        q  : OUT std_logic
    );
END d_latch;

ARCHITECTURE bhv OF d_latch IS
BEGIN
    PROCESS (en, d)
    BEGIN
        IF (en = '1') THEN
            q <= d;
        END IF;
    END PROCESS;
END bhv;

// VHDL entity d_ff, as the project stores it:
LIBRARY ieee;
USE ieee.std_logic_1164.ALL;

ENTITY d_ff IS
    PORT (
        clk : IN  std_logic;
        d   : IN  std_logic;
        q   : OUT std_logic
    );
END d_ff;

ARCHITECTURE bhv OF d_ff IS
BEGIN
    PROCESS (clk)
    BEGIN
        IF rising_edge(clk) THEN
            q <= d;
        END IF;
    END PROCESS;
END bhv;

// VHDL entity jk_ff, as the project stores it:
LIBRARY ieee;
USE ieee.std_logic_1164.ALL;

ENTITY jk_ff IS
    PORT (
        clk : IN  std_logic;
        j   : IN  std_logic;
        k   : IN  std_logic;
        q   : OUT std_logic
    );
END jk_ff;

ARCHITECTURE bhv OF jk_ff IS
    SIGNAL q_internal : std_logic := '0';
BEGIN
    q <= q_internal;

    PROCESS (clk)
    BEGIN
        IF rising_edge(clk) THEN
            IF (j = '0' AND k = '0') THEN
                q_internal <= q_internal;     -- Hold
            ELSIF (j = '0' AND k = '1') THEN
                q_internal <= '0';            -- Reset
            ELSIF (j = '1' AND k = '0') THEN
                q_internal <= '1';            -- Set
            ELSIF (j = '1' AND k = '1') THEN
                q_internal <= NOT q_internal; -- Toggle
            END IF;
        END IF;
    END PROCESS;
END bhv;

// VHDL entity d_ff_async, as the project stores it:
LIBRARY ieee;
USE ieee.std_logic_1164.ALL;

ENTITY d_ff_async IS
    PORT (
        clk : IN  std_logic;
        d   : IN  std_logic;
        clr : IN  std_logic;
        set : IN  std_logic;
        q   : OUT std_logic
    );
END d_ff_async;

ARCHITECTURE bhv OF d_ff_async IS
    SIGNAL q_int : std_logic := '0';
BEGIN
    q <= q_int;

    PROCESS (clk, clr, set)
    BEGIN
        -- 1순위: 비동기 Clear (클럭 무관 즉시 0)
        IF (clr = '1') THEN
            q_int <= '0';
        -- 2순위: 비동기 Set (클럭 무관 즉시 1)
        ELSIF (set = '1') THEN
            q_int <= '1';
        -- 3순위: 동기 D Flip-Flop 동작 (클럭 상승 에지)
        ELSIF rising_edge(clk) THEN
            q_int <= d;
        END IF;
    END PROCESS;
END bhv;
